# Fritzing sketch Infinity Band1 (saved by Fritzing 0.9.1b)
circuit board: 6.01126cm x 6.0777cm
breadboards: 1

parts:
  Part1 = LightBlue Bean
  neopixel1 = Neopixel Ring 12
  S1 = Pushbutton [package="[SMD]"]
  Part2 = Power Cell LiPo Charger/Booster
  U1 = LIPO-110mAh [package=lipo-110]
  U2 = Vibration Motor- ROB-08449 [package=vibe-motor-10mm]
  RGB_SMD_LED1 = SMD RGB LED (WS2812) [package=5050]

nets:
  VCC: Part1.VCC, neopixel1.VCC, RGB_SMD_LED1.VCC
  N1: Part1.D5/SCK, neopixel1.IN
  N2: Part1.D4/MISO, S1.Pin_1, S1.Pin_2
  GND: Part1.GND, neopixel1.GND, S1.Pin_3, S1.Pin_4, Part2.GND, U1.+, U2.+, RGB_SMD_LED1.VSS
  N3: Part1.BAT, Part2.VCC
  N4: neopixel1.OUT, RGB_SMD_LED1.DIn

custom parts:
  Neopixel Ring 12: Neopixel Ring x12
